# Fritzing sketch WiFi RGB Strip (saved by Fritzing 1.0.1rc)
breadboards: 1

parts:
  MH-ET_LIVE_ESP32_DEVKIT1 = MH-ET LIVE ESP32 DEVKIT 38 pins
  Q1 = ULN2803 Darlington Array
  RGB_Strip_LED1 = RGB Strip LED
  JACK1 = 2.1mm Barrel Jack with Terminal Block

nets:
  N1: MH-ET_LIVE_ESP32_DEVKIT1.IO27, Q1.I3
  N2: MH-ET_LIVE_ESP32_DEVKIT1.IO14, Q1.I2
  N3: MH-ET_LIVE_ESP32_DEVKIT1.IO12, Q1.I1
  N4: MH-ET_LIVE_ESP32_DEVKIT1.GND#58, Q1.GND, JACK1.NEG
  N5: Q1.O3, RGB_Strip_LED1.Blue_Connect
  N6: Q1.O2, RGB_Strip_LED1.Red_Connect
  N7: Q1.O1, RGB_Strip_LED1.Green_Connect
  N8: RGB_Strip_LED1.Common_Connect, JACK1.POS

custom parts:
  MH-ET LIVE ESP32 DEVKIT 38 pins: http://mh.nodebb.com/topic/2/mh-et-live-esp32-devkit
  ULN2803 Darlington Array: ULN2803 Darlington Transistor Array with Flyback Protection
  RGB Strip LED: A tri-color Strip LED with red, green and blue. Based on LED SMD 5050 RGB Pin order: common cathode - green - red - blue
